# Fritzing sketch External LED Blink (saved by Fritzing 0.8.3b)
breadboards: 1

parts:
  Netduino1 = Netduino
  LED1 = LED - 3mm [color="Red (633nm)" package="3 mm [THT]"]
  R1 = Resistor [tolerance=±5% resistance=1k package="1206 [SMD]"]

nets:
  N1: Netduino1.D13_SPCK, LED1.anode
  N2: Netduino1.GND, R1.Pin_0
  N3: LED1.cathode, R1.Pin_1
