# Fritzing sketch LM35 - Buzzer (saved by Fritzing 0.8.3b)
breadboards: 1

parts:
  Netduino1 = Netduino
  J1 = Piezo Speaker
  T1 = LM35 Temperature Sensor [package="TO92 [THT]"]

nets:
  N1: Netduino1.Aref, Netduino1.3V3, T1.+Vs
  N2: Netduino1.D9_PWM2, J1.pin2
  GND: Netduino1.GND, J1.pin1, T1.GND
  N3: Netduino1.A0, T1.Vout
