# Fritzing sketch LM35 - Temperature (saved by Fritzing 0.8.3b)
breadboards: 1

parts:
  T1 = LM35 Temperature Sensor [package="TO92 [THT]"]
  Netduino1 = Netduino

nets:
  N1: T1.+Vs, Netduino1.3V3
  N2: T1.Vout, Netduino1.A0
  GND: T1.GND, Netduino1.GND
